# Fritzing sketch schema_platine (saved by Fritzing 0.8.5b)
breadboards: 1

parts:
  S1 = Pushbutton [package="[THT]"]
  S2 = Pushbutton [package="[THT]"]
  R1 = Resistor [tolerance=±5% resistance=220 package=THT]
  R2 = Resistor [tolerance=±5% resistance=220 package=THT]
  LED1 = LED - 5mm [color="Red (633nm)" package="5 mm [THT]"]
  LED2 = LED - 5mm [color="Red (633nm)" package="5 mm [THT]"]
  Composants1 = Arduino Uno (Rev3)

nets:
  N1: S1.Pin_1, S1.Pin_2, R2.Pin_0
  N2: S1.Pin_3, S1.Pin_4, S2.Pin_1, S2.Pin_2, Composants1.D2, Composants1.D4, Composants1.5V
  N3: S2.Pin_3, S2.Pin_4, R1.Pin_1
  N4: R1.Pin_0, R2.Pin_1, LED1.cathode, LED2.cathode, Composants1.GND
  N5: LED1.anode, Composants1.D12/MISO
  N6: LED2.anode, Composants1.D13/SCK
